// Digital circuit KombinatorischeSchaltung.dig as structural Verilog
module KombinatorischeSchaltung (
  input  [7:0] S_equenz,
  output MDR_in,
  output MDR_outOP,
  output MAR_in,
  output IR_in,
  output IR_op_out,
  output IP_in,
  output IP_out,
  output R_in,
  output R_out,
  output [1:0] SR_eq_ROPx,
  output B_in,
  output Y_in,
  output Y_out,
  output A_in,
  output ALU_out,
  output [3:0] F_eq_x,
  output WR,
  output RD,
  output RDY,
  output Ca,
  output _0,
  output out_22,
  output [7:0] NA,
  output R,
  output De,
  output WRDY,
  output MDR_outA0,
  output MDR_outA1,
  output MDR_out
);

  wire demultiplexer_1_out_0, demultiplexer_1_out_1, demultiplexer_1_out_2, demultiplexer_1_out_3,
       demultiplexer_1_out_4, demultiplexer_1_out_5, demultiplexer_1_out_6, demultiplexer_1_out_7,
       demultiplexer_1_out_8, demultiplexer_1_out_9, demultiplexer_1_out_10, demultiplexer_1_out_11,
       demultiplexer_1_out_12, demultiplexer_1_out_13;

  Demultiplexer #(.Selector_Bits(4)) demultiplexer_1 (
    .sel(S_equenz[3:0]), .in(1'b1), .out_0(demultiplexer_1_out_0), .out_1(demultiplexer_1_out_1),
    .out_2(demultiplexer_1_out_2), .out_3(demultiplexer_1_out_3), .out_4(demultiplexer_1_out_4),
    .out_5(demultiplexer_1_out_5), .out_6(demultiplexer_1_out_6), .out_7(demultiplexer_1_out_7),
    .out_8(demultiplexer_1_out_8), .out_9(demultiplexer_1_out_9), .out_10(demultiplexer_1_out_10),
    .out_11(demultiplexer_1_out_11), .out_12(demultiplexer_1_out_12), .out_13(demultiplexer_1_out_13));  // open: out_14, out_15
  assign MDR_in = demultiplexer_1_out_0 ? 1'b1 : 1'bz;  // Driver driver_1
  PullDown pulldown_1 (.out(MDR_in));
  PullDown pulldown_2 (.out(MDR_out));
  PullDown pulldown_3 (.out(MDR_outA1));
  PullDown pulldown_4 (.out(MDR_outA0));
  assign MDR_outOP = demultiplexer_1_out_2 ? 1'b1 : 1'bz;  // Driver driver_2
  PullDown pulldown_5 (.out(MDR_outOP));
  assign MAR_in = demultiplexer_1_out_0 ? 1'b1 : 1'bz;  // Driver driver_3
  PullDown pulldown_6 (.out(MAR_in));
  assign IR_in = demultiplexer_1_out_2 ? 1'b1 : 1'bz;  // Driver driver_4
  PullDown pulldown_7 (.out(IR_in));
  PullDown pulldown_8 (.out(IR_op_out));
  assign IP_in = demultiplexer_1_out_1 ? 1'b1 : 1'bz;  // Driver driver_5
  PullDown pulldown_9 (.out(IP_in));
  assign IP_out = demultiplexer_1_out_0 ? 1'b1 : 1'bz;  // Driver driver_6
  PullDown pulldown_10 (.out(IP_out));
  PullDown pulldown_11 (.out(R_in));
  PullDown pulldown_12 (.out(R_out));
  PullDown #(.Bits(2)) pulldown_13 (.out(SR_eq_ROPx));
  PullDown pulldown_14 (.out(Y_in));
  PullDown pulldown_15 (.out(Y_out));
  PullDown pulldown_16 (.out(B_in));
  assign A_in = demultiplexer_1_out_0 ? 1'b1 : 1'bz;  // Driver driver_7
  PullDown pulldown_17 (.out(A_in));
  assign ALU_out = demultiplexer_1_out_1 ? 1'b1 : 1'bz;  // Driver driver_8
  PullDown pulldown_18 (.out(ALU_out));
  assign F_eq_x = demultiplexer_1_out_0 ? 4'b0110 : 4'bz;  // Driver driver_9
  PullDown #(.Bits(4)) pulldown_19 (.out(F_eq_x));
  PullDown pulldown_20 (.out(Ca));
  PullDown pulldown_21 (.out(_0));
  PullDown pulldown_22 (.out(out_22));
  PullDown pulldown_23 (.out(RDY));
  PullDown pulldown_24 (.out(RD));
  assign RD = demultiplexer_1_out_0 ? 1'b1 : 1'bz;  // Driver driver_10
  PullDown pulldown_25 (.out(WR));
  PullDown #(.Bits(8)) pulldown_26 (.out(NA));
  PullDown pulldown_27 (.out(R));
  PullDown pulldown_28 (.out(De));
  assign De = demultiplexer_1_out_2 ? 1'b1 : 1'bz;  // Driver driver_11
  assign WRDY = demultiplexer_1_out_1 ? 1'b1 : 1'bz;  // Driver driver_12
  PullDown pulldown_29 (.out(WRDY));

  // Notes on the sheet:
  //   0 FETCH
  //   3 ADD R2 = R2 + R1
endmodule
